# Fritzing sketch Untitled Sketch (saved by Fritzing 0.9.1b)
breadboards: 2

parts:
  Part1 = Arduino Mega 2560 (Rev3)
  J1 = Piezo Speaker

nets:
  N1: Part1.D13_PWM, J1.pin1
  N2: Part1.GND, J1.pin2
